// Logisim project Full Substractor.circ as structural Verilog: 1 circuit, main circuit main
module main (
  input  x,
  input  y,
  input  z,
  input  w,
  output D,
  output B
);

  wire and_1_out, and_2_out, not_1_out, not_2_out, xor_1_out;

  not not_1 (not_1_out, x);
  xor xor_1 (xor_1_out, x, y);
  and and_1 (and_1_out, not_1_out, y);
  not not_2 (not_2_out, xor_1_out);
  xor xor_2 (D, xor_1_out, z);
  and and_2 (and_2_out, z, not_2_out);
  or or_1 (B, and_2_out, and_1_out);
endmodule
