// Logisim project JKFF.circ as structural Verilog: 15 circuits, main circuit D Latch
module SR_Latch_NOR (
  input  R_Reset,
  input  S_Set,
  output Q,
  output Q_prime
);

  nor nor_1 (Q, R_Reset, Q_prime);
  nor nor_2 (Q_prime, Q, S_Set);
endmodule

module SR_Latch_NAND (
  input  S_Set,
  input  R_Reset,
  output Q,
  output Q_prime
);

  nand nand_1 (Q, S_Set, Q_prime);
  nand nand_2 (Q_prime, Q, R_Reset);
endmodule

module SR_Latch_with_control_input (
  input  S,
  input  En,
  input  R,
  output Q,
  output Q_prime
);

  wire nand_1_out, nand_2_out;

  nand nand_1 (nand_1_out, S, En);
  nand nand_2 (nand_2_out, En, R);
  nand nand_3 (Q, nand_1_out, Q_prime);
  nand nand_4 (Q_prime, Q, nand_2_out);
endmodule

module D_Latch (
  input  Preset,
  input  D,
  input  En,
  input  Clear,
  output Q,
  output Q_prime
);

  wire nand_1_out, nand_2_out, not_1_out;

  not not_1 (not_1_out, D);
  nand nand_1 (nand_1_out, D, En);
  nand nand_2 (nand_2_out, En, not_1_out);
  nand nand_3 (Q, Preset, nand_1_out, Q_prime);
  nand nand_4 (Q_prime, Q, nand_2_out, Clear);
endmodule

// D-FF
module D_flip_flop (
  input  Preset,
  input  D,
  input  CLK,
  input  Clear,
  output Q,
  output Q_prime
);

  wire d_latch_1_q, not_1_out;

  not not_1 (not_1_out, CLK);
  D_Latch d_latch_1 (.Preset(Preset), .D(D), .Q(d_latch_1_q), .En(not_1_out), .Clear(Clear));  // open: Q_prime
  LED led_1 (.in(d_latch_1_q));
  D_Latch d_latch_2 (.Preset(Preset), .D(d_latch_1_q), .Q(Q), .En(CLK), .Q_prime(Q_prime), .Clear(Clear));
  LED led_2 (.in(Q));
endmodule

module JK_flip_flop (
  input  Preset,
  input  J,
  input  K,
  input  in_4,
  input  Clear,
  output Q,
  output Q_prime
);

  wire and_1_out, and_2_out, not_1_out, or_1_out;

  not not_1 (not_1_out, K);
  and and_1 (and_1_out, Q_prime, J);
  and and_2 (and_2_out, not_1_out, Q);
  or or_1 (or_1_out, and_1_out, and_2_out);
  D_flip_flop d_flip_flop_1 (.Preset(Preset), .Q(Q), .CLK(in_4), .Clear(Clear), .Q_prime(Q_prime), .D(or_1_out));
endmodule

module T_flip_flop (
  input  T,
  input  T_2,
  output Q,
  output Q_prime,
  output Q_2,
  output Q_prime_2
);

  wire xor_1_out;

  xor xor_1 (xor_1_out, Q_2, T_2);
  JK_flip_flop jk_flip_flop_1 (.J(T), .K(T), .Q(Q), .Q_prime(Q_prime));  // open: Preset, Clear, in_4
  D_flip_flop d_flip_flop_1 (.Q(Q_2), .Q_prime(Q_prime_2), .D(xor_1_out));  // open: Preset, CLK, Clear
endmodule

module _4_bit_Shift_Register (
  input  Preset,
  input  D,
  input  Control,
  input  CLK,
  input  Clear,
  output Q
);

  wire and_1_out, d_flip_flop_1_q, d_flip_flop_2_q, d_flip_flop_3_q;

  and and_1 (and_1_out, Control, CLK);
  D_flip_flop d_flip_flop_1 (
    .Preset(Preset), .Q(d_flip_flop_1_q), .CLK(and_1_out), .Clear(Clear), .D(D));  // open: Q_prime
  D_flip_flop d_flip_flop_2 (
    .Preset(Preset), .Q(d_flip_flop_2_q), .CLK(and_1_out), .Clear(Clear), .D(d_flip_flop_1_q));  // open: Q_prime
  D_flip_flop d_flip_flop_3 (
    .Preset(Preset), .Q(d_flip_flop_3_q), .CLK(and_1_out), .Clear(Clear), .D(d_flip_flop_2_q));  // open: Q_prime
  D_flip_flop d_flip_flop_4 (
    .Preset(Preset), .Q(Q), .CLK(and_1_out), .Clear(Clear), .D(d_flip_flop_3_q));  // open: Q_prime
endmodule

module _4_bit_Shift_Register_2 (
  input  Preset,
  input  Control,
  input  Clear,
  output Q
);

  wire and_1_out, CLK_out, d_flip_flop_1_q, d_flip_flop_2_q, d_flip_flop_3_q, shift_register_1_out;

  Random random_1 ();  // open: clk, next, out, clr
  Shift_Register #(.length(10)) shift_register_1 (
    .clk(CLK_out), .out(shift_register_1_out));  // open: shift, in, load, clr, d0, q0, d1, q1, d2, q2, d3, q3, d4, q4, d5, q5, d6, q6, d7, q7, d8, q8, d9, q9
  Clock CLK (.out(CLK_out));
  and and_1 (and_1_out, Control, CLK_out);
  D_flip_flop d_flip_flop_1 (
    .Preset(Preset), .Q(d_flip_flop_1_q), .CLK(and_1_out), .Clear(Clear), .D(shift_register_1_out));  // open: Q_prime
  LED led_1 (.in(d_flip_flop_1_q));
  D_flip_flop d_flip_flop_2 (
    .Preset(Preset), .Q(d_flip_flop_2_q), .CLK(and_1_out), .Clear(Clear), .D(d_flip_flop_1_q));  // open: Q_prime
  LED led_2 (.in(d_flip_flop_2_q));
  D_flip_flop d_flip_flop_3 (
    .Preset(Preset), .Q(d_flip_flop_3_q), .CLK(and_1_out), .Clear(Clear), .D(d_flip_flop_2_q));  // open: Q_prime
  LED led_3 (.in(d_flip_flop_3_q));
  D_flip_flop d_flip_flop_4 (
    .Preset(Preset), .Q(Q), .CLK(and_1_out), .Clear(Clear), .D(d_flip_flop_3_q));  // open: Q_prime
  LED led_4 (.in(Q));
endmodule

module _4_bit_Shift_Register_3_with_RNG (
  input  Preset,
  input  Control,
  input  Clear,
  output Q
);

  wire and_1_out, CLK_out, d_flip_flop_1_q, d_flip_flop_2_q, d_flip_flop_3_q, random_1_out;

  Clock CLK (.out(CLK_out));
  Random #(.width(1)) random_1 (.clk(CLK_out), .out(random_1_out));  // open: next, clr
  and and_1 (and_1_out, Control, CLK_out);
  D_flip_flop d_flip_flop_1 (
    .Preset(Preset), .Q(d_flip_flop_1_q), .CLK(and_1_out), .Clear(Clear), .D(random_1_out));  // open: Q_prime
  D_flip_flop d_flip_flop_2 (
    .Preset(Preset), .Q(d_flip_flop_2_q), .CLK(and_1_out), .Clear(Clear), .D(d_flip_flop_1_q));  // open: Q_prime
  D_flip_flop d_flip_flop_3 (
    .Preset(Preset), .Q(d_flip_flop_3_q), .CLK(and_1_out), .Clear(Clear), .D(d_flip_flop_2_q));  // open: Q_prime
  D_flip_flop d_flip_flop_4 (
    .Preset(Preset), .Q(Q), .CLK(and_1_out), .Clear(Clear), .D(d_flip_flop_3_q));  // open: Q_prime
endmodule

// FA
module Full_Adder (
  input  X,
  input  Y,
  input  Cin,
  output S,
  output Cout
);

  wire and_1_out, and_2_out, xor_1_out;

  xor xor_1 (xor_1_out, X, Y);
  and and_1 (and_1_out, X, Y);
  xor xor_2 (S, xor_1_out, Cin);
  and and_2 (and_2_out, xor_1_out, Cin);
  or or_1 (Cout, and_2_out, and_1_out);
endmodule

module _4_bit_Serial_Adder (
  input  A,
  input  B,
  input  Control,
  input  CLK,
  input  Clear,
  output S
);

  wire and_1_out, d_flip_flop_1_q, full_adder_1_cout, n4_bit_shift_register_1_q, n4_bit_shift_register_2_q;

  _4_bit_Shift_Register u_4_bit_shift_register_1 (
    .CLK(CLK), .Q(n4_bit_shift_register_1_q), .Preset(1'b1), .Clear(Clear), .Control(Control), .D(A));
  _4_bit_Shift_Register u_4_bit_shift_register_2 (
    .CLK(CLK), .Q(n4_bit_shift_register_2_q), .Preset(1'b1), .Clear(Clear), .Control(Control), .D(B));
  and and_1 (and_1_out, Control, CLK);
  D_flip_flop d_flip_flop_1 (
    .Preset(1'b1), .Q(d_flip_flop_1_q), .CLK(and_1_out), .Clear(Clear), .D(full_adder_1_cout));  // open: Q_prime
  Full_Adder full_adder_1 (
    .X(n4_bit_shift_register_1_q), .Y(n4_bit_shift_register_2_q), .Cin(d_flip_flop_1_q), .S(S),
    .Cout(full_adder_1_cout));
endmodule

module _4_bit_Serial_Adder_2 (
  input  Control,
  input  Clear
);

  wire and_1_out, CLK_out, d_flip_flop_1_q, full_adder_1_cout, full_adder_1_s, n4_bit_shift_register_1_q,
       n4_bit_shift_register_2_q, shift_register_1_out, shift_register_2_out;

  Clock CLK (.out(CLK_out));
  Shift_Register #(.length(4)) shift_register_1 (
    .clk(CLK_out), .out(shift_register_1_out));  // open: shift, in, load, clr, d0, q0, d1, q1, d2, q2, d3, q3
  Shift_Register #(.length(4)) shift_register_2 (
    .clk(CLK_out), .out(shift_register_2_out));  // open: shift, in, load, clr, d0, q0, d1, q1, d2, q2, d3, q3
  _4_bit_Shift_Register u_4_bit_shift_register_1 (
    .CLK(CLK_out), .Q(n4_bit_shift_register_1_q), .Preset(1'b1), .Clear(Clear), .Control(Control),
    .D(shift_register_1_out));
  _4_bit_Shift_Register u_4_bit_shift_register_2 (
    .CLK(CLK_out), .Q(n4_bit_shift_register_2_q), .Preset(1'b1), .Clear(Clear), .Control(Control),
    .D(shift_register_2_out));
  and and_1 (and_1_out, Control, CLK_out);
  D_flip_flop d_flip_flop_1 (
    .Preset(1'b1), .Q(d_flip_flop_1_q), .CLK(and_1_out), .Clear(Clear), .D(full_adder_1_cout));  // open: Q_prime
  Full_Adder full_adder_1 (
    .X(n4_bit_shift_register_1_q), .Y(n4_bit_shift_register_2_q), .Cin(d_flip_flop_1_q), .S(full_adder_1_s),
    .Cout(full_adder_1_cout));
  Shift_Register #(.length(4)) shift_register_3 (
    .in(full_adder_1_s), .clk(CLK_out));  // open: shift, out, load, clr, d0, q0, d1, q1, d2, q2, d3, q3
endmodule

module cv (
  input  in_1,
  input  in_2
);

  wire adder_1_cout, adder_1_out, and_1_out, clock_1_out, d_ff_1_q, n4_bit_shift_register_1_q,
       n4_bit_shift_register_2_q, shift_register_1_out, shift_register_2_out;

  Shift_Register #(.length(4)) shift_register_1 (
    .clk(clock_1_out), .out(shift_register_1_out));  // open: shift, in, load, clr, d0, q0, d1, q1, d2, q2, d3, q3
  Shift_Register #(.length(4)) shift_register_2 (
    .clk(clock_1_out), .out(shift_register_2_out));  // open: shift, in, load, clr, d0, q0, d1, q1, d2, q2, d3, q3
  Clock clock_1 (.out(clock_1_out));
  _4_bit_Shift_Register u_4_bit_shift_register_1 (
    .CLK(clock_1_out), .Q(n4_bit_shift_register_1_q), .Preset(1'b1), .Clear(in_2), .Control(in_1),
    .D(shift_register_1_out));
  _4_bit_Shift_Register u_4_bit_shift_register_2 (
    .CLK(clock_1_out), .Q(n4_bit_shift_register_2_q), .Preset(1'b1), .Clear(in_2), .Control(in_1),
    .D(shift_register_2_out));
  and and_1 (and_1_out, in_1, clock_1_out);
  D_Flip_Flop d_ff_1 (.clk(and_1_out), .D(adder_1_cout), .Q(d_ff_1_q), .en(in_2));  // open: Qn, preset, reset
  Shift_Register #(.length(4), .trigger("falling")) shift_register_3 (
    .in(adder_1_out), .clk(clock_1_out));  // open: shift, out, load, clr, d0, q0, d1, q1, d2, q2, d3, q3
  Adder #(.width(1)) adder_1 (
    .a(n4_bit_shift_register_1_q), .b(n4_bit_shift_register_2_q), .out(adder_1_out), .cin(d_ff_1_q),
    .cout(adder_1_cout));
endmodule

module fsdzxf (
  input  in_1,
  input  in_2
);

  wire adder_1_cout, adder_1_out, clock_1_out, j_k_ff_1_q, j_k_ff_1_qn, n4_bit_shift_register_1_q,
       n4_bit_shift_register_2_q, not_1_out, shift_register_1_out, shift_register_2_out;

  Shift_Register #(.length(4)) shift_register_1 (
    .clk(clock_1_out), .out(shift_register_1_out));  // open: shift, in, load, clr, d0, q0, d1, q1, d2, q2, d3, q3
  Shift_Register #(.length(4)) shift_register_2 (
    .clk(clock_1_out), .out(shift_register_2_out));  // open: shift, in, load, clr, d0, q0, d1, q1, d2, q2, d3, q3
  Clock clock_1 (.out(clock_1_out));
  _4_bit_Shift_Register u_4_bit_shift_register_1 (
    .CLK(clock_1_out), .Q(n4_bit_shift_register_1_q), .Preset(1'b1), .Clear(in_2), .Control(in_1),
    .D(shift_register_1_out));
  _4_bit_Shift_Register u_4_bit_shift_register_2 (
    .CLK(clock_1_out), .Q(n4_bit_shift_register_2_q), .Preset(1'b1), .Clear(in_2), .Control(in_1),
    .D(shift_register_2_out));
  J_K_Flip_Flop j_k_ff_1 (
    .J(j_k_ff_1_qn), .clk(clock_1_out), .K(adder_1_cout), .Q(j_k_ff_1_q), .Qn(j_k_ff_1_qn), .en(in_2));  // open: preset, reset
  Shift_Register #(.length(4), .trigger("falling")) shift_register_3 (
    .in(not_1_out), .clk(clock_1_out));  // open: shift, out, load, clr, d0, q0, d1, q1, d2, q2, d3, q3
  Adder #(.width(1)) adder_1 (
    .a(n4_bit_shift_register_1_q), .b(n4_bit_shift_register_2_q), .out(adder_1_out), .cin(j_k_ff_1_q),
    .cout(adder_1_cout));
  not not_1 (not_1_out, adder_1_out);
endmodule
