// Logisim project askhsh 3.circ as structural Verilog: 1 circuit, main circuit main
module main (
  input  b2,
  input  b1,
  input  a1,
  input  a2,
  output out_5,
  output out_6,
  output out_7,
  output out_8
);

  wire and_1_out, and_3_out, and_4_out, and_5_out;

  and and_1 (and_1_out, a2, b2);
  and and_2 (out_7, and_1_out, and_4_out);
  and and_3 (and_3_out, b1, a2);
  xor xor_1 (out_8, and_1_out, and_4_out);
  and and_4 (and_4_out, and_3_out, and_5_out);
  and and_5 (and_5_out, b2, a1);
  xor xor_2 (out_6, and_5_out, and_3_out);
  and and_6 (out_5, a1, b1);
endmodule
