// Logisim project decoder 4-16.circ as structural Verilog: 1 circuit, main circuit main
module main (
  input  in_1,
  input  in_2,
  input  in_3,
  input  in_4,
  output out_5,
  output out_6,
  output out_7,
  output out_8,
  output out_9,
  output out_10,
  output out_11,
  output out_12,
  output out_13,
  output out_14,
  output out_15,
  output out_16,
  output out_17,
  output out_18,
  output out_19,
  output out_20
);

  wire not_1_out, not_2_out, not_3_out, not_4_out, not_5_out, not_6_out, not_7_out;

  not not_1 (not_1_out, in_1);
  not not_2 (not_2_out, in_2);
  not not_3 (not_3_out, in_3);
  not not_4 (not_4_out, in_1);
  not not_5 (not_5_out, in_2);
  not not_6 (not_6_out, in_3);
  not not_7 (not_7_out, in_4);
  and and_1 (out_5, in_4, not_1_out, not_3_out, not_2_out);
  and and_2 (out_6, in_4, not_3_out, in_1, not_2_out);
  and and_3 (out_7, in_4, in_2, not_1_out, not_3_out);
  and and_4 (out_8, in_4, not_3_out, in_1, in_2);
  and and_5 (out_9, in_4, not_1_out, not_2_out, in_3);
  and and_6 (out_10, in_4, in_1, in_3, not_2_out);
  and and_7 (out_11, in_4, not_1_out, in_3, in_2);
  and and_8 (out_12, in_4, in_1, in_3, in_2);
  and and_9 (out_13, not_7_out, not_4_out, not_6_out, not_5_out);
  and and_10 (out_14, not_7_out, not_6_out, in_1, not_5_out);
  and and_11 (out_15, not_7_out, in_2, not_4_out, not_6_out);
  and and_12 (out_16, not_7_out, not_6_out, in_1, in_2);
  and and_13 (out_17, not_7_out, not_4_out, not_5_out, in_3);
  and and_14 (out_18, not_7_out, in_1, in_3, not_5_out);
  and and_15 (out_19, not_7_out, not_4_out, in_3, in_2);
  and and_16 (out_20, not_7_out, in_1, in_3, in_2);
endmodule
