// Logisim project ergasia eksaminou1.circ as structural Verilog: 14 circuits, main circuit D Latch
module D_Latch (
  input  Preset,
  input  D,
  input  En,
  input  Clear,
  output Q,
  output Q_prime
);

  wire nand_1_out, nand_2_out, not_1_out;

  not not_1 (not_1_out, D);
  nand nand_1 (nand_1_out, D, En);
  nand nand_2 (nand_2_out, En, not_1_out);
  nand nand_3 (Q, Preset, nand_1_out, Q_prime);
  nand nand_4 (Q_prime, Q, nand_2_out, Clear);
endmodule

// D-FF
module D_flip_flop_negative_edge_triggered (
  input  Preset,
  input  D,
  input  CLK,
  input  Clear,
  output Q,
  output Q_prime
);

  wire d_latch_1_q, not_1_out;

  not not_1 (not_1_out, CLK);
  D_Latch d_latch_1 (.Preset(Preset), .D(D), .Q(d_latch_1_q), .En(CLK), .Clear(Clear));  // open: Q_prime
  LED led_1 (.in(d_latch_1_q));
  D_Latch d_latch_2 (.Preset(Preset), .D(d_latch_1_q), .Q(Q), .En(not_1_out), .Q_prime(Q_prime), .Clear(Clear));
  LED led_2 (.in(Q));
endmodule

module JK_flip_flop (
  input  Preset,
  input  J,
  input  K,
  input  in_4,
  input  Clear,
  output Q,
  output Q_prime
);

  wire and_1_out, and_2_out, not_1_out, or_1_out;

  not not_1 (not_1_out, K);
  and and_1 (and_1_out, Q_prime, J);
  and and_2 (and_2_out, not_1_out, Q);
  or or_1 (or_1_out, and_1_out, and_2_out);
  D_flip_flop_negative_edge_triggered d_flip_flop_negative_edge_triggered_1 (
    .Preset(Preset), .Q(Q), .CLK(in_4), .Clear(Clear), .Q_prime(Q_prime), .D(or_1_out));
endmodule

module T_flip_flop_with_JKff (
  input  Preset,
  input  T,
  input  Clock,
  input  Clear,
  output Q,
  output Q_prime
);

  JK_flip_flop jk_flip_flop_1 (.J(T), .K(T), .Q(Q), .Q_prime(Q_prime), .Preset(Preset), .Clear(Clear), .in_4(Clock));
endmodule

module _4bit_Ripple_Counter_with_Tff (
  input  Constant_Logic_1,
  input  Reset,
  output A0,
  output A1,
  output A2,
  output A3
);

  wire clock_1_out;

  Clock clock_1 (.out(clock_1_out));
  T_flip_flop_with_JKff t_flip_flop_with_jkff_1 (
    .T(Constant_Logic_1), .Q(A0), .Preset(1'b1), .Clear(Reset), .Clock(clock_1_out));  // open: Q_prime
  T_flip_flop_with_JKff t_flip_flop_with_jkff_2 (
    .T(Constant_Logic_1), .Q(A1), .Preset(1'b1), .Clear(Reset), .Clock(A0));  // open: Q_prime
  T_flip_flop_with_JKff t_flip_flop_with_jkff_3 (
    .T(Constant_Logic_1), .Q(A2), .Preset(1'b1), .Clear(Reset), .Clock(A1));  // open: Q_prime
  T_flip_flop_with_JKff t_flip_flop_with_jkff_4 (
    .T(Constant_Logic_1), .Q(A3), .Preset(1'b1), .Clear(Reset), .Clock(A2));  // open: Q_prime
endmodule

module _4bit_Ripple_Counter_with_Dff (
  input  Reset,
  output A0,
  output A1,
  output A2,
  output A3
);

  wire clock_1_out, d_flip_flop_negative_edge_triggered_1_q_prime,
       d_flip_flop_negative_edge_triggered_2_q_prime, d_flip_flop_negative_edge_triggered_3_q_prime,
       d_flip_flop_negative_edge_triggered_4_q_prime;

  Clock clock_1 (.out(clock_1_out));
  D_flip_flop_negative_edge_triggered d_flip_flop_negative_edge_triggered_1 (
    .Preset(1'b1), .Q(A0), .CLK(clock_1_out), .Clear(Reset),
    .Q_prime(d_flip_flop_negative_edge_triggered_1_q_prime), .D(d_flip_flop_negative_edge_triggered_1_q_prime));
  D_flip_flop_negative_edge_triggered d_flip_flop_negative_edge_triggered_2 (
    .Preset(1'b1), .Q(A1), .CLK(A0), .Clear(Reset), .Q_prime(d_flip_flop_negative_edge_triggered_2_q_prime),
    .D(d_flip_flop_negative_edge_triggered_2_q_prime));
  D_flip_flop_negative_edge_triggered d_flip_flop_negative_edge_triggered_3 (
    .Preset(1'b1), .Q(A2), .CLK(A1), .Clear(Reset), .Q_prime(d_flip_flop_negative_edge_triggered_3_q_prime),
    .D(d_flip_flop_negative_edge_triggered_3_q_prime));
  D_flip_flop_negative_edge_triggered d_flip_flop_negative_edge_triggered_4 (
    .Preset(1'b1), .Q(A3), .CLK(A2), .Clear(Reset), .Q_prime(d_flip_flop_negative_edge_triggered_4_q_prime),
    .D(d_flip_flop_negative_edge_triggered_4_q_prime));
endmodule

module _4bit_Synchronous_Counter (
  input  Const_1,
  input  in_2,
  input  in_3,
  input  in_4,
  input  in_5,
  output out_6,
  output out_7,
  output out_8,
  output out_9
);

  wire and_1_out, and_2_out, and_3_out, and_4_out, clock_1_out;

  and and_1 (and_1_out, Const_1, out_6);
  and and_2 (and_2_out, and_1_out, out_7);
  and and_3 (and_3_out, and_2_out, out_8);
  Clock clock_1 (.out(clock_1_out));
  JK_flip_flop jk_flip_flop_1 (
    .J(Const_1), .K(Const_1), .Q(out_6), .Preset(1'b1), .Clear(in_2), .in_4(clock_1_out));  // open: Q_prime
  JK_flip_flop jk_flip_flop_2 (
    .J(and_1_out), .K(and_1_out), .Q(out_7), .Preset(1'b1), .Clear(in_3), .in_4(clock_1_out));  // open: Q_prime
  JK_flip_flop jk_flip_flop_3 (
    .J(and_2_out), .K(and_2_out), .Q(out_8), .Preset(1'b1), .Clear(in_4), .in_4(clock_1_out));  // open: Q_prime
  JK_flip_flop jk_flip_flop_4 (
    .J(and_3_out), .K(and_3_out), .Q(out_9), .Preset(1'b1), .Clear(in_5), .in_4(clock_1_out));  // open: Q_prime
  and and_4 (and_4_out, out_9, and_3_out);
endmodule

module _4bit_up_down_synchronous_counter_JKff (
  input  in_1,
  input  in_2,
  input  in_3,
  input  in_4,
  input  in_5,
  input  in_6,
  input  in_7,
  input  in_8,
  input  in_9,
  input  in_10,
  input  in_11,
  input  in_12,
  input  in_13,
  output out_14,
  output out_15,
  output out_16,
  output out_17,
  output out_18,
  output out_19,
  output out_20,
  output out_21,
  output out_22
);

  wire and_1_out, and_2_out, and_3_out, and_4_out, and_5_out, and_6_out, and_7_out, and_8_out, and_9_out,
       and_10_out, and_11_out, and_12_out, and_13_out, and_14_out, and_15_out, and_16_out, clock_1_out,
       clock_2_out, jk_flip_flop_1_q_prime, jk_flip_flop_2_q_prime, jk_flip_flop_3_q_prime, not_1_out,
       not_2_out, or_1_out, or_2_out, or_3_out, or_4_out, or_5_out, or_6_out, or_7_out, or_8_out, or_9_out,
       t_flip_flop_with_jkff_1_q_prime, t_flip_flop_with_jkff_2_q_prime, t_flip_flop_with_jkff_3_q_prime,
       t_flip_flop_with_jkff_4_q_prime;

  not not_1 (not_1_out, in_1);
  and and_1 (and_1_out, not_1_out, in_3);
  and and_2 (and_2_out, and_1_out, jk_flip_flop_1_q_prime);
  and and_3 (and_3_out, and_2_out, jk_flip_flop_2_q_prime);
  and and_4 (and_4_out, and_3_out, jk_flip_flop_3_q_prime);
  and and_5 (and_5_out, in_1, out_14);
  and and_6 (and_6_out, and_5_out, out_16);
  and and_7 (and_7_out, and_6_out, out_18);
  or or_1 (or_1_out, in_1, and_1_out);
  or or_2 (or_2_out, and_5_out, and_2_out);
  or or_3 (or_3_out, and_6_out, and_3_out);
  or or_4 (or_4_out, and_7_out, and_4_out);
  Clock clock_1 (.out(clock_1_out));
  JK_flip_flop jk_flip_flop_1 (
    .J(or_1_out), .K(or_1_out), .Q(out_14), .Q_prime(jk_flip_flop_1_q_prime), .Preset(1'b1), .Clear(in_6),
    .in_4(clock_1_out));
  JK_flip_flop jk_flip_flop_2 (
    .J(or_2_out), .K(or_2_out), .Q(out_16), .Q_prime(jk_flip_flop_2_q_prime), .Preset(1'b1), .Clear(in_8),
    .in_4(clock_1_out));
  JK_flip_flop jk_flip_flop_3 (
    .J(or_3_out), .K(or_3_out), .Q(out_18), .Q_prime(jk_flip_flop_3_q_prime), .Preset(1'b1), .Clear(in_10),
    .in_4(clock_1_out));
  JK_flip_flop jk_flip_flop_4 (
    .J(or_4_out), .K(or_4_out), .Q(out_20), .Preset(1'b1), .Clear(in_12), .in_4(clock_1_out));  // open: Q_prime
  not not_2 (not_2_out, in_2);
  and and_8 (and_8_out, not_2_out, in_4);
  and and_9 (and_9_out, and_8_out, t_flip_flop_with_jkff_1_q_prime);
  and and_10 (and_10_out, and_9_out, t_flip_flop_with_jkff_2_q_prime);
  and and_11 (and_11_out, in_2, out_15);
  and and_12 (and_12_out, and_11_out, out_17);
  and and_13 (and_13_out, and_10_out, t_flip_flop_with_jkff_3_q_prime);
  and and_14 (and_14_out, and_13_out, t_flip_flop_with_jkff_4_q_prime);
  or or_5 (or_5_out, in_2, and_8_out);
  or or_6 (or_6_out, and_11_out, and_9_out);
  or or_7 (or_7_out, and_12_out, and_10_out);
  and and_15 (and_15_out, and_12_out, out_19);
  or or_8 (or_8_out, and_15_out, and_13_out);
  and and_16 (and_16_out, and_15_out, out_21);
  or or_9 (or_9_out, and_16_out, and_14_out);
  Clock clock_2 (.out(clock_2_out));
  T_flip_flop_with_JKff t_flip_flop_with_jkff_1 (
    .T(or_5_out), .Q(out_15), .Q_prime(t_flip_flop_with_jkff_1_q_prime), .Preset(1'b1), .Clear(in_5),
    .Clock(clock_2_out));
  T_flip_flop_with_JKff t_flip_flop_with_jkff_2 (
    .T(or_6_out), .Q(out_17), .Q_prime(t_flip_flop_with_jkff_2_q_prime), .Preset(1'b1), .Clear(in_7),
    .Clock(clock_2_out));
  T_flip_flop_with_JKff t_flip_flop_with_jkff_3 (
    .T(or_7_out), .Q(out_19), .Q_prime(t_flip_flop_with_jkff_3_q_prime), .Preset(1'b1), .Clear(in_9),
    .Clock(clock_2_out));
  T_flip_flop_with_JKff t_flip_flop_with_jkff_4 (
    .T(or_8_out), .Q(out_21), .Q_prime(t_flip_flop_with_jkff_4_q_prime), .Preset(1'b1), .Clear(in_11),
    .Clock(clock_2_out));
  T_flip_flop_with_JKff t_flip_flop_with_jkff_5 (
    .T(or_9_out), .Q(out_22), .Preset(1'b1), .Clear(in_13), .Clock(clock_2_out));  // open: Q_prime
endmodule

module _2_4_Decoder (
  input  E,
  input  A0,
  input  A1,
  output D0,
  output D1,
  output D2,
  output D3
);

  wire not_1_out, not_2_out;

  not not_1 (not_1_out, A0);
  not not_2 (not_2_out, A1);
  and and_1 (D0, E, not_1_out, not_2_out);
  and and_2 (D1, E, A0, not_2_out);
  and and_3 (D2, E, not_1_out, A1);
  and and_4 (D3, E, A0, A1);
endmodule

module _2_1_Tristate_MUX (
  input  A,
  input  B,
  input  S,
  output Y
);

  wire not_1_out;

  not not_1 (not_1_out, S);
  assign Y = not_1_out ? A : 1'bz;  // Controlled_Buffer controlled_buffer_1
  assign Y = S ? B : 1'bz;  // Controlled_Buffer controlled_buffer_2
endmodule

module _4_1_Tristate_MUX (
  input  D0,
  input  D1,
  input  D2,
  input  D3,
  input  S0,
  input  S1,
  input  E,
  output Y
);

  wire n2_4_decoder_1_d0, n2_4_decoder_1_d1, n2_4_decoder_1_d2, n2_4_decoder_1_d3;

  assign Y = n2_4_decoder_1_d0 ? D0 : 1'bz;  // Controlled_Buffer controlled_buffer_1
  assign Y = n2_4_decoder_1_d1 ? D1 : 1'bz;  // Controlled_Buffer controlled_buffer_2
  _2_4_Decoder u_2_4_decoder_1 (
    .E(S0), .A0(S1), .A1(E), .D0(n2_4_decoder_1_d0), .D1(n2_4_decoder_1_d1), .D2(n2_4_decoder_1_d2),
    .D3(n2_4_decoder_1_d3));
  assign Y = n2_4_decoder_1_d2 ? D2 : 1'bz;  // Controlled_Buffer controlled_buffer_3
  assign Y = n2_4_decoder_1_d3 ? D3 : 1'bz;  // Controlled_Buffer controlled_buffer_4
endmodule

module asd (
  input  in_1,
  input  in_2,
  output out_3,
  output out_4,
  output out_5,
  output out_6,
  output out_7
);

  wire clock_1_out;

  Clock clock_1 (.out(clock_1_out));
  JK_flip_flop jk_flip_flop_1 (
    .J(in_1), .K(in_1), .Q(out_3), .Preset(1'b1), .Clear(in_2), .in_4(clock_1_out));  // open: Q_prime
  JK_flip_flop jk_flip_flop_2 (
    .J(in_1), .K(in_1), .Q(out_4), .Preset(1'b1), .Clear(in_2), .in_4(out_3));  // open: Q_prime
  JK_flip_flop jk_flip_flop_3 (
    .J(in_1), .K(in_1), .Q(out_5), .Preset(1'b1), .Clear(in_2), .in_4(out_4));  // open: Q_prime
  JK_flip_flop jk_flip_flop_4 (
    .J(in_1), .K(in_1), .Q(out_6), .Preset(1'b1), .Clear(in_2), .in_4(out_5));  // open: Q_prime
  JK_flip_flop jk_flip_flop_5 (
    .J(in_1), .K(in_1), .Q(out_7), .Preset(1'b1), .Clear(in_2), .in_4(out_6));  // open: Q_prime
endmodule

module sdf (
  input  in_1,
  input  in_2,
  input  in_3,
  input  in_4,
  input  in_5,
  output out_6,
  output out_7,
  output out_8,
  output out_9,
  output out_10
);

  wire and_1_out, and_2_out, and_3_out, clock_1_out, d_flip_flop_negative_edge_triggered_1_q_prime,
       xor_1_out, xor_2_out, xor_3_out, xor_4_out;

  Clock clock_1 (.out(clock_1_out));
  D_flip_flop_negative_edge_triggered d_flip_flop_negative_edge_triggered_1 (
    .Preset(1'b1), .Q(out_6), .CLK(clock_1_out), .Clear(in_1),
    .Q_prime(d_flip_flop_negative_edge_triggered_1_q_prime), .D(d_flip_flop_negative_edge_triggered_1_q_prime));
  xor xor_1 (xor_1_out, out_6, out_7);
  D_flip_flop_negative_edge_triggered d_flip_flop_negative_edge_triggered_2 (
    .Preset(1'b1), .Q(out_7), .CLK(clock_1_out), .Clear(in_2), .D(xor_1_out));  // open: Q_prime
  xor xor_2 (xor_2_out, and_1_out, out_8);
  D_flip_flop_negative_edge_triggered d_flip_flop_negative_edge_triggered_3 (
    .Preset(1'b1), .Q(out_8), .CLK(clock_1_out), .Clear(in_3), .D(xor_2_out));  // open: Q_prime
  xor xor_3 (xor_3_out, and_2_out, out_9);
  D_flip_flop_negative_edge_triggered d_flip_flop_negative_edge_triggered_4 (
    .Preset(1'b1), .Q(out_9), .CLK(clock_1_out), .Clear(in_4), .D(xor_3_out));  // open: Q_prime
  xor xor_4 (xor_4_out, and_3_out, out_10);
  D_flip_flop_negative_edge_triggered d_flip_flop_negative_edge_triggered_5 (
    .Preset(1'b1), .Q(out_10), .CLK(clock_1_out), .Clear(in_5), .D(xor_4_out));  // open: Q_prime
  and and_1 (and_1_out, out_7, out_6);
  and and_2 (and_2_out, out_8, and_1_out);
  and and_3 (and_3_out, out_9, and_2_out);
endmodule

module tff_ergasia_eksaminou (
  input  in_1,
  input  in_2,
  input  in_3,
  input  in_4,
  input  in_5,
  input  in_6,
  input  in_7,
  output out_8,
  output out_9,
  output out_10,
  output out_11,
  output out_12
);

  wire and_1_out, and_2_out, and_3_out, and_4_out, and_5_out, and_6_out, and_7_out, and_8_out, and_9_out,
       clock_1_out, not_1_out, or_1_out, or_2_out, or_3_out, or_4_out, or_5_out,
       t_flip_flop_with_jkff_1_q_prime, t_flip_flop_with_jkff_2_q_prime, t_flip_flop_with_jkff_3_q_prime,
       t_flip_flop_with_jkff_4_q_prime;

  not not_1 (not_1_out, in_1);
  and and_1 (and_1_out, not_1_out, in_2);
  and and_2 (and_2_out, and_1_out, t_flip_flop_with_jkff_1_q_prime);
  and and_3 (and_3_out, and_2_out, t_flip_flop_with_jkff_2_q_prime);
  and and_4 (and_4_out, and_3_out, t_flip_flop_with_jkff_3_q_prime);
  and and_5 (and_5_out, and_4_out, t_flip_flop_with_jkff_4_q_prime);
  and and_6 (and_6_out, in_1, out_8);
  and and_7 (and_7_out, and_6_out, out_9);
  and and_8 (and_8_out, and_7_out, out_10);
  and and_9 (and_9_out, and_8_out, out_11);
  or or_1 (or_1_out, in_1, and_1_out);
  or or_2 (or_2_out, and_6_out, and_2_out);
  or or_3 (or_3_out, and_7_out, and_3_out);
  or or_4 (or_4_out, and_8_out, and_4_out);
  or or_5 (or_5_out, and_9_out, and_5_out);
  Clock clock_1 (.out(clock_1_out));
  T_flip_flop_with_JKff t_flip_flop_with_jkff_1 (
    .T(or_1_out), .Q(out_8), .Q_prime(t_flip_flop_with_jkff_1_q_prime), .Preset(1'b1), .Clear(in_3),
    .Clock(clock_1_out));
  T_flip_flop_with_JKff t_flip_flop_with_jkff_2 (
    .T(or_2_out), .Q(out_9), .Q_prime(t_flip_flop_with_jkff_2_q_prime), .Preset(1'b1), .Clear(in_4),
    .Clock(clock_1_out));
  T_flip_flop_with_JKff t_flip_flop_with_jkff_3 (
    .T(or_3_out), .Q(out_10), .Q_prime(t_flip_flop_with_jkff_3_q_prime), .Preset(1'b1), .Clear(in_5),
    .Clock(clock_1_out));
  T_flip_flop_with_JKff t_flip_flop_with_jkff_4 (
    .T(or_4_out), .Q(out_11), .Q_prime(t_flip_flop_with_jkff_4_q_prime), .Preset(1'b1), .Clear(in_6),
    .Clock(clock_1_out));
  T_flip_flop_with_JKff t_flip_flop_with_jkff_5 (
    .T(or_5_out), .Q(out_12), .Preset(1'b1), .Clear(in_7), .Clock(clock_1_out));  // open: Q_prime
endmodule
