// Logisim project ergasia eksaminou2.circ as structural Verilog: 1 circuit, main circuit main
module main (
  input  S0,
  input  S2,
  input  S1,
  input  a1,
  input  b1,
  input  a0,
  input  b0,
  input  Cin,
  input  Cin_2,
  output out_10,
  output Cout,
  output out_12,
  output Cout_2
);

  wire and_1_out, and_2_out, and_3_out, and_4_out, and_5_out, and_6_out, and_7_out, and_8_out, and_9_out,
       and_10_out, and_11_out, and_12_out, and_13_out, and_14_out, and_15_out, and_16_out, and_17_out,
       and_18_out, nand_1_out, nand_2_out, not_1_out, not_2_out, not_3_out, not_4_out, not_5_out, not_6_out,
       not_7_out, not_8_out, not_9_out, not_10_out, not_11_out, not_12_out, or_1_out, or_2_out, xor_1_out,
       xor_2_out, xor_3_out, xor_4_out, xor_5_out, xor_6_out;

  not not_1 (not_1_out, a0);
  and and_1 (and_1_out, a0, b0);
  or or_1 (or_1_out, a0, b0);
  xor xor_1 (xor_1_out, a0, b0);
  nand nand_1 (nand_1_out, a0, b0);
  not not_2 (not_2_out, a1);
  and and_2 (and_2_out, a1, b1);
  or or_2 (or_2_out, a1, b1);
  xor xor_2 (xor_2_out, a1, b1);
  nand nand_2 (nand_2_out, a1, b1);
  not not_3 (not_3_out, a0);
  not not_4 (not_4_out, a1);
  xor xor_3 (xor_3_out, a0, b0);
  and and_3 (and_3_out, not_3_out, b0);
  xor xor_4 (xor_4_out, a1, b1);
  and and_4 (and_4_out, not_4_out, b1);
  not not_5 (not_5_out, xor_3_out);
  not not_6 (not_6_out, xor_4_out);
  xor xor_5 (xor_5_out, xor_3_out, Cin);
  and and_5 (and_5_out, Cin, not_5_out);
  xor xor_6 (xor_6_out, xor_4_out, Cin_2);
  and and_6 (and_6_out, Cin_2, not_6_out);
  or or_3 (Cout, and_5_out, and_3_out);
  or or_4 (Cout_2, and_6_out, and_4_out);
  not not_7 (not_7_out, S2);
  not not_8 (not_8_out, S2);
  not not_9 (not_9_out, S1);
  not not_10 (not_10_out, S1);
  not not_11 (not_11_out, S0);
  not not_12 (not_12_out, S0);
  and and_7 (and_7_out, not_7_out, not_9_out, not_11_out, not_1_out);
  and and_8 (and_8_out, not_7_out, not_9_out, S0, and_1_out);
  and and_9 (and_9_out, not_7_out, S1, not_11_out, or_1_out);
  and and_10 (and_10_out, not_7_out, S1, S0, xor_1_out);
  and and_11 (and_11_out, S2, not_9_out, not_11_out, nand_1_out);
  and and_12 (and_12_out, S2, not_9_out, S0, xor_5_out);
  and and_13 (and_13_out, not_8_out, not_10_out, not_12_out, not_2_out);
  and and_14 (and_14_out, not_8_out, not_10_out, S0, and_2_out);
  and and_15 (and_15_out, not_8_out, S1, not_12_out, or_2_out);
  and and_16 (and_16_out, not_8_out, S1, S0, xor_2_out);
  and and_17 (and_17_out, S2, not_10_out, not_12_out, nand_2_out);
  and and_18 (and_18_out, S2, not_10_out, S0, xor_6_out);
  or or_5 (out_10, and_7_out, and_8_out, and_9_out, and_10_out, and_11_out, and_12_out);
  or or_6 (out_12, and_13_out, and_14_out, and_15_out, and_16_out, and_17_out, and_18_out);
endmodule
