// Logisim project multiplexer.circ as structural Verilog: 1 circuit, main circuit main
module main (
  input  in_1,
  input  a0,
  input  b0,
  input  a1,
  input  b1,
  input  a2,
  input  b2,
  input  a3,
  input  b3,
  input  a4,
  input  b4,
  input  a5,
  input  b5,
  input  a6,
  input  b6,
  input  a7,
  input  b7,
  output out_18,
  output out_19,
  output out_20,
  output out_21,
  output out_22,
  output out_23,
  output out_24,
  output out_25
);

  wire and_1_out, and_2_out, and_3_out, and_4_out, and_5_out, and_6_out, and_7_out, and_8_out, and_9_out,
       and_10_out, and_11_out, and_12_out, and_13_out, and_14_out, and_15_out, and_16_out, not_1_out;

  not not_1 (not_1_out, in_1);
  and and_1 (and_1_out, a0, in_1);
  and and_2 (and_2_out, not_1_out, b0);
  and and_3 (and_3_out, a1, in_1);
  and and_4 (and_4_out, not_1_out, b1);
  and and_5 (and_5_out, a2, in_1);
  and and_6 (and_6_out, not_1_out, b2);
  and and_7 (and_7_out, a3, in_1);
  and and_8 (and_8_out, not_1_out, b3);
  and and_9 (and_9_out, a4, in_1);
  and and_10 (and_10_out, not_1_out, b4);
  and and_11 (and_11_out, a5, in_1);
  and and_12 (and_12_out, not_1_out, b5);
  and and_13 (and_13_out, a6, in_1);
  and and_14 (and_14_out, not_1_out, b6);
  and and_15 (and_15_out, a7, in_1);
  and and_16 (and_16_out, not_1_out, b7);
  or or_1 (out_18, and_1_out, and_2_out);
  or or_2 (out_19, and_3_out, and_4_out);
  or or_3 (out_20, and_5_out, and_6_out);
  or or_4 (out_21, and_7_out, and_8_out);
  or or_5 (out_22, and_9_out, and_10_out);
  or or_6 (out_23, and_11_out, and_12_out);
  or or_7 (out_24, and_13_out, and_14_out);
  or or_8 (out_25, and_15_out, and_16_out);
endmodule
