// Logisim project multiplier 4 bit.circ as structural Verilog: 1 circuit, main circuit main
module main (
  input  in_1,
  input  in_2,
  input  in_3,
  input  in_4,
  input  Y0,
  input  Y2,
  input  Cin,
  input  Y3,
  input  Y1,
  input  Cin_2,
  input  Cin_3,
  input  in_12,
  output P4,
  output P5,
  output P6,
  output P0,
  output P1,
  output P7,
  output P2,
  output P3
);

  wire and_1_out, and_2_out, and_3_out, and_4_out, and_5_out, and_6_out, and_7_out, and_9_out, and_10_out,
       and_11_out, and_12_out, and_13_out, and_14_out, and_15_out, and_16_out, and_17_out, and_18_out,
       and_19_out, and_20_out, and_21_out, and_22_out, and_23_out, and_24_out, and_25_out, and_26_out,
       and_27_out, and_28_out, and_29_out, and_30_out, and_31_out, and_32_out, and_33_out, and_34_out,
       and_35_out, and_36_out, and_37_out, and_38_out, and_39_out, and_40_out, or_1_out, or_2_out, or_3_out,
       or_4_out, or_5_out, or_6_out, or_7_out, or_8_out, or_9_out, or_10_out, or_11_out, xor_1_out,
       xor_2_out, xor_3_out, xor_4_out, xor_5_out, xor_6_out, xor_7_out, xor_8_out, xor_10_out, xor_11_out,
       xor_12_out, xor_13_out, xor_14_out, xor_15_out, xor_16_out, xor_17_out, xor_18_out, xor_19_out,
       xor_20_out, xor_22_out, xor_23_out, xor_24_out, xor_25_out, xor_26_out, xor_27_out, xor_28_out,
       xor_29_out, xor_30_out, xor_31_out, xor_32_out;

  and and_1 (and_1_out, Y1, in_1);
  and and_2 (and_2_out, in_2, Y1);
  and and_3 (and_3_out, in_3, Y1);
  and and_4 (and_4_out, in_4, Y1);
  and and_5 (and_5_out, Y0, in_1);
  and and_6 (and_6_out, Y0, in_2);
  and and_7 (and_7_out, Y0, in_3);
  and and_8 (P0, in_4, Y0);
  xor xor_1 (xor_1_out, Cin, and_6_out);
  or or_1 (or_1_out, and_9_out, and_13_out);
  xor xor_2 (xor_2_out, Cin, in_12);
  or or_2 (or_2_out, and_10_out, and_14_out);
  xor xor_3 (xor_3_out, Cin, and_3_out);
  or or_3 (or_3_out, and_11_out, and_15_out);
  xor xor_4 (xor_4_out, Cin, and_1_out);
  or or_4 (or_4_out, and_12_out, and_16_out);
  xor xor_5 (xor_5_out, and_7_out, xor_1_out);
  and and_9 (and_9_out, and_7_out, xor_1_out);
  xor xor_6 (xor_6_out, and_5_out, xor_2_out);
  and and_10 (and_10_out, and_5_out, xor_2_out);
  xor xor_7 (xor_7_out, and_4_out, xor_3_out);
  and and_11 (and_11_out, and_4_out, xor_3_out);
  xor xor_8 (xor_8_out, and_2_out, xor_4_out);
  and and_12 (and_12_out, and_2_out, xor_4_out);
  xor xor_9 (P1, xor_5_out, Cin);
  and and_13 (and_13_out, Cin, xor_5_out);
  xor xor_10 (xor_10_out, xor_6_out, or_1_out);
  and and_14 (and_14_out, or_1_out, xor_6_out);
  xor xor_11 (xor_11_out, xor_7_out, or_2_out);
  and and_15 (and_15_out, or_2_out, xor_7_out);
  xor xor_12 (xor_12_out, xor_8_out, or_3_out);
  and and_16 (and_16_out, or_3_out, xor_8_out);
  and and_17 (and_17_out, Y2, in_1);
  and and_18 (and_18_out, in_2, Y2);
  and and_19 (and_19_out, in_3, Y2);
  and and_20 (and_20_out, in_4, Y2);
  xor xor_13 (xor_13_out, Cin_2, xor_11_out);
  or or_5 (or_5_out, and_21_out, and_25_out);
  xor xor_14 (xor_14_out, Cin_2, or_4_out);
  or or_6 (or_6_out, and_22_out, and_26_out);
  xor xor_15 (xor_15_out, Cin_2, and_19_out);
  or or_7 (or_7_out, and_23_out, and_27_out);
  xor xor_16 (xor_16_out, Cin_2, and_17_out);
  or or_8 (or_8_out, and_24_out, and_28_out);
  xor xor_17 (xor_17_out, xor_10_out, xor_13_out);
  and and_21 (and_21_out, xor_10_out, xor_13_out);
  xor xor_18 (xor_18_out, xor_12_out, xor_14_out);
  and and_22 (and_22_out, xor_12_out, xor_14_out);
  xor xor_19 (xor_19_out, and_20_out, xor_15_out);
  and and_23 (and_23_out, and_20_out, xor_15_out);
  xor xor_20 (xor_20_out, and_18_out, xor_16_out);
  and and_24 (and_24_out, and_18_out, xor_16_out);
  xor xor_21 (P2, xor_17_out, Cin_2);
  and and_25 (and_25_out, Cin_2, xor_17_out);
  xor xor_22 (xor_22_out, xor_18_out, or_5_out);
  and and_26 (and_26_out, or_5_out, xor_18_out);
  xor xor_23 (xor_23_out, xor_19_out, or_6_out);
  and and_27 (and_27_out, or_6_out, xor_19_out);
  xor xor_24 (xor_24_out, xor_20_out, or_7_out);
  and and_28 (and_28_out, or_7_out, xor_20_out);
  and and_29 (and_29_out, in_2, Y3);
  and and_30 (and_30_out, Y3, in_1);
  and and_31 (and_31_out, in_3, Y3);
  and and_32 (and_32_out, in_4, Y3);
  or or_9 (or_9_out, and_33_out, and_37_out);
  xor xor_25 (xor_25_out, Cin_3, xor_23_out);
  xor xor_26 (xor_26_out, Cin_3, or_8_out);
  or or_10 (or_10_out, and_34_out, and_38_out);
  xor xor_27 (xor_27_out, Cin_3, and_31_out);
  or or_11 (or_11_out, and_35_out, and_39_out);
  xor xor_28 (xor_28_out, Cin_3, and_30_out);
  or or_12 (P7, and_36_out, and_40_out);
  and and_33 (and_33_out, xor_22_out, xor_25_out);
  xor xor_29 (xor_29_out, xor_22_out, xor_25_out);
  xor xor_30 (xor_30_out, xor_24_out, xor_26_out);
  and and_34 (and_34_out, xor_24_out, xor_26_out);
  xor xor_31 (xor_31_out, and_32_out, xor_27_out);
  and and_35 (and_35_out, and_32_out, xor_27_out);
  xor xor_32 (xor_32_out, and_29_out, xor_28_out);
  and and_36 (and_36_out, and_29_out, xor_28_out);
  xor xor_33 (P3, xor_29_out, Cin_3);
  and and_37 (and_37_out, Cin_3, xor_29_out);
  xor xor_34 (P4, xor_30_out, or_9_out);
  and and_38 (and_38_out, or_9_out, xor_30_out);
  xor xor_35 (P5, xor_31_out, or_10_out);
  and and_39 (and_39_out, or_10_out, xor_31_out);
  xor xor_36 (P6, xor_32_out, or_11_out);
  and and_40 (and_40_out, or_11_out, xor_32_out);
endmodule
