// Logisim project ασκηση 2.circ as structural Verilog: 1 circuit, main circuit main
module main (
  input  Cin,
  input  x0,
  input  y0,
  input  x1,
  input  y1,
  input  x2,
  input  y2,
  input  x3,
  input  y3,
  output S0,
  output S1,
  output S2,
  output S3,
  output Cout
);

  wire and_1_out, and_2_out, and_3_out, and_4_out, and_5_out, and_6_out, and_7_out, and_8_out, or_1_out,
       or_2_out, or_3_out, or_4_out, xor_1_out, xor_2_out, xor_3_out, xor_4_out, xor_5_out, xor_6_out,
       xor_7_out, xor_8_out;

  xor xor_1 (xor_1_out, Cin, y0);
  or or_1 (or_1_out, and_1_out, and_5_out);
  xor xor_2 (xor_2_out, Cin, y1);
  or or_2 (or_2_out, and_2_out, and_6_out);
  or or_3 (or_3_out, and_3_out, and_7_out);
  or or_4 (or_4_out, and_4_out, and_8_out);
  xor xor_3 (xor_3_out, Cin, y2);
  xor xor_4 (xor_4_out, Cin, y3);
  xor xor_5 (xor_5_out, x0, xor_1_out);
  and and_1 (and_1_out, x0, xor_1_out);
  xor xor_6 (xor_6_out, x1, xor_2_out);
  and and_2 (and_2_out, x1, xor_2_out);
  xor xor_7 (xor_7_out, x2, xor_3_out);
  and and_3 (and_3_out, x2, xor_3_out);
  xor xor_8 (xor_8_out, x3, xor_4_out);
  and and_4 (and_4_out, x3, xor_4_out);
  xor xor_9 (S0, xor_5_out, Cin);
  and and_5 (and_5_out, Cin, xor_5_out);
  xor xor_10 (S1, xor_6_out, or_1_out);
  and and_6 (and_6_out, or_1_out, xor_6_out);
  xor xor_11 (S2, xor_7_out, or_2_out);
  and and_7 (and_7_out, or_2_out, xor_7_out);
  xor xor_12 (S3, xor_8_out, or_3_out);
  and and_8 (and_8_out, or_3_out, xor_8_out);
endmodule
